# Fritzing sketch Element_scheme_DMXControl (saved by Fritzing 0.9.3b)

parts:
  Часть1 = Arduino Nano (Rev3.0)
  OLED_I2C1 = OLED 128x64 I2C Monochrome Display
  RE1 = KY-040 Rotary encoder [package=THT]
  RS485_module1 = RS485 Module (MAX3485)
  M1 = MT3608 Module
  M2 = TP4056 Module [part_number=HW-107]
  BATT1 = LiPoly Battery (1300mAh)
  S1 = Toggle Switch [package=THT]
  XLR1 = XLR3_NCFAH2 [package=xlr3_nc3fah2]  # not connected

nets:
  GND: Часть1.GND, OLED_I2C1.GND, RE1.GND, RS485_module1.GND, M1.pin4
  N1: Часть1.D2, RE1.CLK
  N2: Часть1.D3, RE1.DT
  N3: Часть1.D4, RE1.SW
  N4: Часть1.D9, RS485_module1.DI
  N5: Часть1.VIN, M1.pin3
  5V: Часть1.5V, OLED_I2C1.VDD, RE1.Vcc, RS485_module1.DE
  N6: Часть1.A6, Часть1.A5, OLED_I2C1.SCK
  N7: Часть1.A4, Часть1.A3, OLED_I2C1.SDA
  N8: M1.pin1, M2.OUT-#1
  N9: M1.pin2, S1.L1
  N10: M2.BAT-, BATT1.negative
  N11: M2.BAT+, BATT1.positive
  N12: M2.OUT-#4, S1.COM

notes:
  max485 to XLR:
  GND - 1
  A - 2
  B - 3

custom parts:
  KY-040 Rotary encoder: KY-040 Rotary Encoder with switch on breakout borad from AZ Delivery
  RS485 Module (MAX3485): Commercially available RS485 to RS232 TTL Module
  MT3608 Module: MT3608 Boost Converter Module Links: Aerosemi MT3608 2A Step Up Converter datasheet
  TP4056 Module: TP4056 Lithium Battery Charge Management Module Links: TP4056 website
  LiPoly Battery (1300mAh): Lithium Ion Polymer Battery (1300mAh)
